# Fritzing sketch TempHumidityDisplay (saved by Fritzing 0.8.7b)
breadboards: 1

parts:
  Part1 = Arduino Uno (Rev3)
  LCD1 = LCD screen
  S1 = Pushbutton [package="[THT]"]
  DHT1 = DHT22 Humidity and Temperature Sensor
  R1 = Resistor [tolerance=±5% resistance=220 package=THT]
  R2 = Resistor [tolerance=±5% resistance=560 package=THT]
  D1 = Rectifier Diode [part_number=1N4001 package="300 mil [THT]"]
  Q1 = PNP-Transistor [package="TO92 [THT]"]

nets:
  N1: Part1.D8, LCD1.E
  N2: Part1.D9_PWM, LCD1.DB4
  N3: Part1.D10_PWM/SS, LCD1.DB5
  N4: Part1.D11_PWM/MOSI, LCD1.DB6
  N5: Part1.D12/MISO, LCD1.DB7
  GND: Part1.GND, LCD1.VSS, LCD1.R/W, S1.Pin_3, S1.Pin_4, DHT1.GND, Q1.E
  N6: Part1.D3_PWM, R2.Pin_0
  N7: Part1.D4, S1.Pin_1, S1.Pin_2
  N8: Part1.D5_PWM, DHT1.DATA, R1.Pin_1
  N9: Part1.D6_PWM, LCD1.V0
  N10: Part1.D7, LCD1.RS
  VDD: Part1.5V, LCD1.VDD, LCD1.LED+, DHT1.VDD, R1.Pin_0, D1.cathode
  N11: LCD1.LED-, D1.anode, Q1.C
  N12: R2.Pin_1, Q1.B
